# Fritzing sketch PMsensor(GP2Y1014) (saved by Fritzing 0.8.7b)
breadboards: 1

parts:
  부품1 = Arduino Uno (Rev3)
  C1 = Electrolytic Capacitor [capacitance=1µF package="100 mil [THT, electrolytic]"]
  R1 = Resistor [tolerance=±1% resistance=10M package=THT]
  U1 = Sharp Dust Sensor [part_number=GP2Y1010AU0F]

nets:
  N1: 부품1.A0, U1.Vo
  N2: 부품1.D2, U1.LED
  N3: C1.-, U1.LED-GND, U1.S-GND
  N4: C1.+, R1.Pin_0, U1.V-LED
  N5: R1.Pin_1, U1.VCC

custom parts:
  Sharp Dust Sensor: Sharp GP2Y1010AU0F Dust Sensor
