# Fritzing sketch PMsensor_RGB (saved by Fritzing 0.8.7b)
breadboards: 1

parts:
  부품1 = Arduino Uno (Rev3)
  C1 = Electrolytic Capacitor [capacitance=1µF package="100 mil [THT, electrolytic]"]
  R1 = Resistor [tolerance=±1% resistance=10M package=THT]
  U1 = Sharp Dust Sensor [part_number=GP2Y1010AU0F]
  LED1 = RGB LED - (4 legs) [package="5 mm [THT]"]
  R2 = Resistor [tolerance=±5% resistance=330 package=THT]

nets:
  N1: 부품1.A0, U1.Vo
  N2: 부품1.D2, U1.LED
  N3: 부품1.D3_PWM, LED1.red_cathode
  N4: 부품1.D5_PWM, LED1.green_cathode
  N5: 부품1.D6_PWM, LED1.blue_cathode
  5V: 부품1.5V, R1.Pin_1, U1.VCC, R2.Pin_0
  N6: 부품1.GND, C1.-, U1.LED-GND, U1.S-GND
  N7: C1.+, R1.Pin_0, U1.V-LED
  N8: LED1.common_anode, R2.Pin_1

custom parts:
  Sharp Dust Sensor: Sharp GP2Y1010AU0F Dust Sensor
